# Fritzing sketch Circuit_layout (saved by Fritzing 0.9.2b)

parts:
  Raspberry_Pi1 = Raspberry Pi 2
  LCD1 = LCD screen
  LCM1602_IIC1 = LCM1602 IIC [part_number="LCM1602 IIC" chip_label="LCM1602 IIC" package="DIP (Dual Inline) [THT]"]
  DS2 = DS18B20 1-Wire Temperature Sensor Probe Cable  # not connected
  DS3 = DS18B20 1-Wire Temperature Sensor Probe Cable  # not connected
  DS4 = DS18B20 1-Wire Temperature Sensor Probe Cable  # not connected
  DS5 = DS18B20 1-Wire Temperature Sensor Probe Cable  # not connected

nets:
  N1: Raspberry_Pi1.GPIO2, LCM1602_IIC1.SDA
  N2: Raspberry_Pi1.GPIO3, LCM1602_IIC1.SCL
  GND: Raspberry_Pi1.GND, LCM1602_IIC1.GND
  5V: Raspberry_Pi1.5V, LCM1602_IIC1.VCC
  VSS: LCD1.VSS, LCM1602_IIC1.VSS
  VDD: LCD1.VDD, LCM1602_IIC1.VDD
  N3: LCD1.V0, LCM1602_IIC1.V0
  N4: LCD1.RS, LCM1602_IIC1.RS
  N5: LCD1.R/W, LCM1602_IIC1.RW
  N6: LCD1.E, LCM1602_IIC1.E
  N7: LCD1.DB0, LCM1602_IIC1.D0
  N8: LCD1.DB1, LCM1602_IIC1.D1
  N9: LCD1.DB2, LCM1602_IIC1.D2
  N10: LCD1.DB3, LCM1602_IIC1.D3
  N11: LCD1.DB4, LCM1602_IIC1.D4
  N12: LCD1.DB5, LCM1602_IIC1.D5
  N13: LCD1.DB6, LCM1602_IIC1.D6
  N14: LCD1.DB7, LCM1602_IIC1.D7
  N15: LCD1.LED+, LCM1602_IIC1.A
  N16: LCD1.LED-, LCM1602_IIC1.K
  N17: LCM1602_IIC1.LED_A, LCM1602_IIC1.LED_B

custom parts:
  LCM1602 IIC: I2C-Module to use a 1602 or 2004 LCD on with the wire.h libory Serial LCD Modul
